# Fritzing sketch Final build (saved by Fritzing 0.9.10b)
breadboards: 1

parts:
  Bauteil3 = LCD1602-I2C
  Bauteil4 = Arduino Nano (Rev3.0)
  TTP223B2 = TTP223B Capacitive Touch Sensor Module
  M2 = Humidity and Temperature Sensor DHT11
  Capacitive_Soil_Moisture_Sensor1 = DFRobot Capacitive Soil Moisture Sensor V1.0 [part_number=SEN0193]
  KY-1 = Keyes Relay [package=THT]
  KY-2 = Keyes Relay [package=THT]
  Capacitive_Soil_Moisture_Sensor2 = DFRobot Capacitive Soil Moisture Sensor V1.0 [part_number=SEN0193]

nets:
  GND: Bauteil3.GND, Bauteil4.GND, TTP223B2.GND, M2.GND, Capacitive_Soil_Moisture_Sensor1.GND, KY-1.ground, KY-2.ground, Capacitive_Soil_Moisture_Sensor2.GND
  VCC: Bauteil3.VCC, Bauteil4.5V, TTP223B2.VCC, M2.Vcc, Capacitive_Soil_Moisture_Sensor1.VCC, KY-1.power, KY-2.power, Capacitive_Soil_Moisture_Sensor2.VCC
  N1: Bauteil3.SDA, Bauteil4.A4
  N2: Bauteil3.SCL, Bauteil4.A5
  N3: Bauteil4.D2, KY-1.signal
  N4: Bauteil4.D3, KY-2.signal
  N5: Bauteil4.D6, TTP223B2.SIG
  N6: Bauteil4.D10, M2.Data
  N7: Bauteil4.A7, Capacitive_Soil_Moisture_Sensor2.A
  N8: Bauteil4.A3, Capacitive_Soil_Moisture_Sensor1.A

notes:
  | | | |
  VCC Data NC GND

custom parts:
  LCD1602-I2C: A standard character display, usually with 2x16 characters. Comes in many colors with LCM1602 IIC attached.
  TTP223B Capacitive Touch Sensor Module: The TTP223B capacitive touch sensor module uses the TTP223B IC. The appropriate voltage is approximately 2 to 5.5 volts.
  Humidity and Temperature Sensor DHT11: Digital relative humidity & temperature sensor DHT11
  DFRobot Capacitive Soil Moisture Sensor V1.0: DFRobot Capacitive Soil Moisture Sensor V1.0 This product measures soil moisture levels by capacitive sensing, rather than resistive sensing like other types of moisture sensor. It is made of a corrosion resistant material giving it a long service life. Insert it into soil and impress your friends with the real-time soil moisture data! The product includes an on-board voltage regulator which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
  Keyes Relay: The Keyes 5V relay module is suitable for SCM development, home appliance control. It uses a 5V~12V TIL control signal which can control DC / AC signal.
